// Logisim project cpu.circ as structural Verilog: 1 circuit, main circuit cpu
module cpu (
  input  clk,
  input  [31:0] INSTRUCTION,
  input  [31:0] READ_DATA,
  output [31:0] WRITE_ADDRESS,
  output [31:0] PROGRAM_COUNTER,
  output [31:0] ra,
  output [31:0] sp,
  output [31:0] t0,
  output [31:0] t1,
  output [31:0] t2,
  output [31:0] s0,
  output [31:0] s1,
  output [31:0] a0,
  output [31:0] tohost,
  output [3:0] WRITE_ENABLE,
  output [31:0] WRITE_DATA
);

  wire ASel, BrEq, BrLt, BrUn, BSel, CSRSel, CSRWen, MemRW, PCSel, RegWEn;
  wire [1:0] WBSel;
  wire [2:0] ImmSel;
  wire [3:0] ALUSel;
  wire [31:0] adder_1_out, adder_2_out, ALU_OUTPUT, IMME, INST_ID, multiplexer_1_out, multiplexer_2_out,
       multiplexer_3_out, PC_ID, rs1, rs2, WRITE_BACK;

  Register #(.width(32)) PC (.D(multiplexer_1_out), .clk(clk), .Q(PROGRAM_COUNTER));  // open: en, clr
  Multiplexer #(.enable("false"), .width(32)) multiplexer_1 (
    .in0(adder_1_out), .in1(WRITE_BACK), .out(multiplexer_1_out), .sel(1'b0));
  Register #(.width(32)) register_1 (.D(INSTRUCTION), .clk(clk), .Q(INST_ID));  // open: en, clr
  control_logic control_logic_1 (
    .CSRWen(CSRWen), .PCSel(PCSel), .RegWEn(RegWEn), .ImmSel(ImmSel), .BrUn(BrUn), .ASel(ASel), .BSel(BSel),
    .ALUSel(ALUSel), .MemRW(MemRW), .WBSel(WBSel), .CSRSel(CSRSel), .inst(INSTRUCTION), .BrEq(BrEq),
    .BrLt(BrLt));
  Adder #(.width(32)) adder_1 (.a(32'h4), .b(PROGRAM_COUNTER), .out(adder_1_out));  // open: cin, cout
  Register #(.width(32)) register_2 (.D(PROGRAM_COUNTER), .clk(clk), .Q(PC_ID));  // open: en, clr
  regfile regfile_1 (
    .rs1(INST_ID[19:15]), .rs2(INST_ID[24:20]), .rd(INST_ID[11:7]), .Write_Data(WRITE_BACK), .RegWEn(1'b1),
    .clk(clk), .ra(ra), .sp(sp), .t0(t0), .t1(t1), .t2(t2), .s0(s0), .s1(s1), .a0(a0), .Read_Data_1(rs1),
    .Read_Data_2(rs2));
  csr csr_1 (.tohost(tohost));  // open: CSR_address, CSR_din, CSR_WE, clk
  Multiplexer #(.enable("false"), .width(32)) multiplexer_2 (
    .in0(PC_ID), .in1(rs1), .out(multiplexer_2_out), .sel(1'b1));
  Multiplexer #(.enable("false"), .width(32)) multiplexer_3 (
    .in0(rs2), .in1(IMME), .out(multiplexer_3_out), .sel(1'b1));
  branch_comp branch_comp_1 (.rs1(rs1), .rs2(rs2), .BrUn(BrUn), .BrEq(BrEq), .BrLt(BrLt));
  imm_gen imm_gen_1 (.inst(INST_ID), .ImmSel(ImmSel), .imm(IMME));
  alu alu_1 (.Result(ALU_OUTPUT), .A(multiplexer_2_out), .B(multiplexer_3_out), .ALUSel(4'b0000));
  Adder #(.width(32)) adder_2 (.a(PC_ID), .b(32'h4), .out(adder_2_out));  // open: cin, cout
  Multiplexer #(.enable("false"), .select(2), .width(32)) multiplexer_4 (
    .in0(READ_DATA), .in1(ALU_OUTPUT), .in2(adder_2_out), .out(WRITE_BACK), .sel(2'b01));  // open: in3

  // Other names for the same wires on the sheet: RW[4:0] = INST_ID[11:7]; RA_t[4:0] = INST_ID[19:15];
  //   RB[4:0] = INST_ID[24:20]

  // Notes on the sheet:
  //   Output to IMEM
  //   IF
  //   IMEM (do **NOT** move this)
  //   Inputs from IMEM
  //   ID
  //   Inputs/Outputs for testing. Do **NOT** move these.
  //   EX
  //   WB
  //   Outputs To DMEM
  //   DMEM (do **NOT** move this)
  //   Inputs From DMEM
endmodule
